# Fritzing sketch Wetterstation (saved by Fritzing 0.7.12b)
breadboards: 1

parts:
  Q1 = NPN-Transistor [part_number=S9015 package="TO92 [THT]"]
  XTAL1 = Crystal [frequency="16 Mhz" package=THT]
  U1 = Voltage Regulator - 5V [package="TO220 [THT]"]
  D1 = Rectifier Diode [part_number=1N4001 package="300 mil [THT]"]
  C1 = Electrolytic Capacitor [capacitance=10µF voltage=50V package="100 mil [THT, electrolytic]"]
  S1 = Pushbutton [package="[THT]"]
  LED1 = LED - 5mm [color="Green (555nm)" package="5 mm [THT]"]
  C2 = Electrolytic Capacitor [capacitance=10µF package="100 mil [THT, electrolytic]"]
  LED2 = LED - 5mm [color="Red (633nm)" package="5 mm [THT]"]
  C4 = Ceramic Disk Capacitor [package=THT]
  S2 = Pushbutton [package="[THT]"]
  IC2 = IC, DIP package, 8 pins [chip_label=ATtiny85]
  IC3 = IC, DIP package, 28 pins [chip_label=ATmega328p]
  R2 = Resistor [tolerance=±5% resistance=100k package=THT]
  R6 = Resistor [tolerance=±5% resistance=470 package=THT]
  R7 = Resistor [tolerance=±5% resistance=470 package=THT]
  R4 = Resistor [tolerance=±5% resistance=10k package=THT]
  R3 = Resistor [tolerance=±5% resistance=10k package=THT]
  R1 = Resistor [tolerance=±5% resistance=100k package=THT]
  R5 = Resistor [tolerance=±5% resistance=10k package=THT]
  R9 = Resistor [tolerance=±5% resistance=10k package=THT]
  R8 = Resistor [tolerance=±5% resistance=10k package=THT]
  R10 = Resistor [tolerance=±5% resistance=10k package=THT]
  R11 = Resistor [tolerance=±5% resistance=1k package=THT]
  LED3 = LED - 5mm [color="Green (555nm)" package="5 mm [THT]"]
  R12 = Resistor [tolerance=±5% resistance=470 package=THT]
  R13 = Resistor [tolerance=±5% resistance=1k package=THT]
  R14 = Resistor [tolerance=±5% resistance=1k package=THT]
  R15 = Resistor [tolerance=±5% resistance=1k package=THT]
  R16 = Resistor [tolerance=±5% resistance=1k package=THT]
  R17 = Resistor [tolerance=±5% resistance=1k package=THT]
  R18 = Resistor [tolerance=±5% resistance=1k package=THT]
  IC4 = IC, DIP package, 8 pins [chip_label=IC]
  C5 = Ceramic Capacitor [package=THT]
  R19 = Resistor [tolerance=±5% resistance=18k package=THT]
  C6 = Ceramic Capacitor [package=THT]
  R20 = Resistor [tolerance=±5% resistance=18k package=THT]
  R21 = Resistor [tolerance=±5% resistance=100k package=THT]
  C7 = Ceramic Capacitor [package=THT]
  R22 = Resistor [tolerance=±5% resistance=10M package=THT]
  U3 = mystery part, 3 pins [chip_label=Light part_number=Lichtsensor]
  C8 = Ceramic Capacitor [package=THT]
  U4 = mystery part, 2 pins [chip_label=Hum part_number=Feuchtigkeitssensor]
  U5 = mystery part, 4 pins [chip_label=BT part_number=Bluetooth]
  U6 = mystery part, 2 pins [chip_label=BAT]
  U7 = mystery part, 8 pins [chip_label="SD Module"]
  U8 = mystery part, 4 pins [chip_label=DCF77 part_number="DCF77 receiver"]
  U10 = mystery part, 2 pins [chip_label=Tmp part_number=Temparaturwiderstand]
  R23 = Resistor [tolerance=±5% resistance=470 package=THT]
  U9 = mystery part, 18 pins [chip_label=ILC-Board]
  R24 = Resistor [tolerance=±5% resistance=18k package=THT]
  U11 = mystery part, 6 pins [chip_label=Programmer]
  U12 = mystery part, 3 pins [chip_label=HALL part_number=Hallsensor]
  U13 = mystery part, 3 pins [chip_label=HALL part_number=Hallsensor]
  C3 = Ceramic Disk Capacitor [package=THT]

nets:
  5V: Q1.E, U1.output_voltage, LED1.anode, C2.+, S2.Pin_3, S2.Pin_4, IC2.pin8, IC3.pin7, IC3.pin20, IC3.pin21, R3.Pin_1, U7.pin6, U9.pin1, U11.pin5
  N1: Q1.B, R4.Pin_1
  N2: Q1.C, U5.pin4
  N3: XTAL1.pin_0, IC3.pin10, C3.pin_0
  N4: XTAL1.pin_1, C4.pin_0, IC3.pin9
  N5: U1.input_voltage, D1.cathode, C1.+
  GND: U1.GND, C1.-, S1.Pin_1, S1.Pin_2, C2.-, C4.pin_1, IC2.pin4, IC3.pin8, IC3.pin22, R2.Pin_1, R6.Pin_0, R7.Pin_0, R5.Pin_0, R10.Pin_1, R11.Pin_0, R12.Pin_0, R13.Pin_0, R16.Pin_1, IC4.pin1, C5.pin_1, C6.pin_1, R22.Pin_0, U3.pin2, C8.pin_1, U4.pin2, U5.pin3, U6.pin1, U7.pin1, U7.pin8, U8.pin2, U10.pin1, R23.Pin_0, U9.pin16, U11.pin6, U12.pin2, U13.pin2, C3.pin_1
  N6: D1.anode, R1.Pin_1, U6.pin2
  N7: S1.Pin_3, S1.Pin_4, IC3.pin1, R3.Pin_0, U11.pin2
  N8: LED1.cathode, R6.Pin_1
  N9: LED2.cathode, R7.Pin_1
  N10: LED2.anode, IC3.pin23
  N11: S2.Pin_1, S2.Pin_2, IC3.pin15, R11.Pin_1
  N12: IC2.pin2, U8.pin3
  N13: IC2.pin3, IC3.pin5, LED3.anode
  N14: IC3.pin2, U5.pin2
  N15: IC3.pin3, U5.pin1
  N16: IC3.pin4, R4.Pin_0, R5.Pin_1
  N17: IC3.pin6, R9.Pin_0
  N18: IC3.pin12, U9.pin8
  N19: IC3.pin13, R14.Pin_1
  N20: IC3.pin14, R18.Pin_0
  N21: IC3.pin16, U7.pin5
  N22: IC3.pin17, U7.pin4, U11.pin1
  N23: IC3.pin18, U7.pin2, U11.pin4
  N24: IC3.pin19, U7.pin3, U11.pin3
  3.3V: IC3.pin27, IC4.pin4, IC4.pin8, C5.pin_0, R19.Pin_0, C6.pin_0, R20.Pin_1, U3.pin3, C8.pin_0, U8.pin1, U9.pin17, R24.Pin_1, U12.pin1, U13.pin1
  N25: IC3.pin28, R2.Pin_0, R1.Pin_0
  N26: R9.Pin_1, R8.Pin_1, U8.pin4
  N27: R8.Pin_0, R10.Pin_0
  N28: LED3.cathode, R12.Pin_1
  N29: R13.Pin_1, R15.Pin_1
  N30: R14.Pin_0, R15.Pin_0, U9.pin7
  N31: R16.Pin_0, R17.Pin_0
  N32: R17.Pin_1, R18.Pin_1, U9.pin9
  N33: IC4.pin2, IC4.pin6, R21.Pin_1, C7.pin_0
  N34: IC4.pin3, R21.Pin_0, U9.pin6
  N35: R19.Pin_1, U9.pin5, U12.pin3
  N36: R20.Pin_0, U9.pin4, U13.pin3
  N37: C7.pin_1, R22.Pin_1, U4.pin1
  N38: U3.pin1, R23.Pin_1, U9.pin11
  N39: U10.pin2, U9.pin10, R24.Pin_0
